# Fritzing sketch WiFi Module (saved by Fritzing 0.9.3b)
circuit board: 8.82601cm x 4.33379cm

parts:
  Part1 = NRF24L01+ Breakout Board
  U1 = ESP8266 NodeMCU LoLin module
  J1 = male pin header, 8 pins [form="♂ (male)"]
  C1 = Electrolytic Capacitor [capacitance=10nF package="100 mil [THT, electrolytic]"]
  C2 = Ceramic Capacitor [capacitance=0.1nF package="100 mil [THT, multilayer]"]
  J2 = male pin header, 10 pins [form="♂ (male)"]
  S1 = Pushbutton [package="[THT]"]
  S2 = Pushbutton [package="[THT]"]
  R1 = Resistor [tolerance=±5% resistance=10k package=THT]
  R2 = Resistor [tolerance=±5% resistance=10k package=THT]

nets:
  GND: Part1.GND, U1.GND, C1.-, C2.0, J2.pin10, R1.Pin_1, R2.Pin_1
  VCC: Part1.VCC, U1.3V3, C1.+, C2.1, S1.Pin_3, S1.Pin_4, S2.Pin_3, S2.Pin_4
  N1: Part1.CE, U1.D4
  N2: Part1.CS, U1.D2
  N3: Part1.SCK, U1.D5
  N4: Part1.MOSI, U1.D7
  N5: Part1.MISO, U1.D6
  N6: U1.D0, S1.Pin_1, S1.Pin_2, R1.Pin_0
  N7: U1.D1, S2.Pin_1, S2.Pin_2, R2.Pin_0
  N8: U1.RX, J2.pin5
  N9: U1.TX, J2.pin6
  N10: U1.Vin, J1.pin1

notes:
  GND
  TX / RX
  5V
  10nF
  0.1nF
  NRF24L01

custom parts:
  ESP8266 NodeMCU LoLin module: ESP8266 based NodeMCU
